// Digital circuit lab2_part2.dig as structural Verilog
module lab2_part2 (
  input  in0,
  input  in1,
  input  in2,
  input  in3,
  output seg_a,
  output seg_f,
  output seg_b,
  output seg_g,
  output seg_e,
  output seg_c,
  output seg_d,
  output seg_dp,
  output sign_a,
  output sign_f,
  output sign_b,
  output sign_g,
  output sign_e,
  output sign_c,
  output sign_d,
  output sign_dp
);

  wire [2:0] not_1_out;
  wire [3:0] add_1_s, multiplexer_1_out;

  Seven_Seg seven_seg_1 (.a(1'b0), .b(1'b0), .c(1'b0), .d(1'b0), .e(1'b0), .f(1'b0), .g(in3), .dp(1'b0));
  Seven_Seg seven_seg_2 (.a(seg_a), .b(seg_b), .c(seg_c), .d(seg_d), .e(seg_e), .f(seg_f), .g(seg_g), .dp(1'b0));
  not not_1 (not_1_out[0], in0);
  not not_2 (not_1_out[1], in1);
  not not_3 (not_1_out[2], in2);
  Add #(.Bits(4)) add_1 (.a({1'b0, not_1_out}), .b(4'b0001), .c_i(1'b0), .s(add_1_s));  // open: c_o
  Multiplexer #(.Bits(4)) multiplexer_1 (
    .sel(in3), .in_0({in3, in2, in1, in0}), .in_1(add_1_s), .out(multiplexer_1_out));
  Multiplexer #(.Selector_Bits(4), .Bits(7)) multiplexer_2 (
    .sel(multiplexer_1_out), .in_0(7'b0111111), .in_1(7'b0000110), .in_2(7'b1011011), .in_3(7'b1001111),
    .in_4(7'b1100110), .in_5(7'b1101101), .in_6(7'b1111101), .in_7(7'b0000111), .in_8({7{1'b1}}),
    .in_9({7{1'b0}}), .in_10({7{1'b0}}), .in_11({7{1'b0}}), .in_12({7{1'b0}}), .in_13({7{1'b0}}),
    .in_14({7{1'b0}}), .in_15({7{1'b0}}), .out({seg_g, seg_f, seg_e, seg_d, seg_c, seg_b, seg_a}));

  assign seg_dp = 1'b0;
  assign sign_a = 1'b0;
  assign sign_b = 1'b0;
  assign sign_c = 1'b0;
  assign sign_d = 1'b0;
  assign sign_dp = 1'b0;
  assign sign_e = 1'b0;
  assign sign_f = 1'b0;
  assign sign_g = in3;

  // Notes on the sheet:
  //   Interface (do not edit the content inside this box)
  //   Outputs:
  //   Inputs
  //   Sign
  //   Decimal Number
endmodule

/* Test case:
in3 in2 in1 in0  sign_a sign_b sign_c sign_d sign_e sign_f sign_g  seg_a seg_b seg_c seg_d seg_e seg_f seg_g
 0   0   0   0    0      0      0      0      0      0      0       1     1     1     1     1     1     0
*/
