// Digital circuit lab2_part3.dig as structural Verilog
module lab2_part3 (
  input  clk,
  input  in0,
  input  in1,
  input  in2,
  input  in3,
  input  sel_write_1,
  input  sel_write_0,
  input  sel_readA_1,
  input  sel_readA_0,
  input  sel_readB_1,
  input  sel_readB_0,
  output out0,
  output out1,
  output out2,
  output out3,
  output reg0_0,
  output reg0_1,
  output reg0_2,
  output reg0_3,
  output reg1_0,
  output reg1_1,
  output reg1_2,
  output reg1_3,
  output reg2_0,
  output reg2_1,
  output reg2_2,
  output reg2_3,
  output reg3_0,
  output reg3_1,
  output reg3_2,
  output reg3_3,
  output inA_0,
  output inA_1,
  output inA_2,
  output inA_3,
  output inB_0,
  output inB_1,
  output inB_2,
  output inB_3
);

  wire en_0, en_1, en_2, en_3;
  wire [3:0] multiplexer_1_out, multiplexer_2_out;
  wire [7:0] reg_1_q, reg_2_q, reg_3_q, reg_4_q;

  Seven_Seg_Hex seven_seg_hex_1 (.d({inA_3, inA_2, inA_1, inA_0}), .dp(1'b0));
  Seven_Seg_Hex seven_seg_hex_2 (.d({reg3_3, reg3_2, reg3_1, reg3_0}), .dp(1'b0));
  Seven_Seg_Hex seven_seg_hex_3 (.d({in3, in2, in1, in0}), .dp(1'b0));
  Seven_Seg_Hex seven_seg_hex_4 (.d({inB_3, inB_2, inB_1, inB_0}), .dp(1'b0));
  Seven_Seg_Hex seven_seg_hex_5 (.d({reg2_3, reg2_2, reg2_1, reg2_0}), .dp(1'b0));
  Seven_Seg_Hex seven_seg_hex_6 (.d({2'b00, sel_write_1, sel_write_0}), .dp(1'b0));
  Seven_Seg_Hex seven_seg_hex_7 (.d({2'b00, sel_readA_1, sel_readA_0}), .dp(1'b0));
  Seven_Seg_Hex seven_seg_hex_8 (.d({out3, out2, out1, out0}), .dp(1'b0));
  Decoder #(.Selector_Bits(2)) decoder_1 (
    .sel({sel_write_1, sel_write_0}), .out_0(en_0), .out_1(en_1), .out_2(en_2), .out_3(en_3));
  Seven_Seg_Hex seven_seg_hex_9 (.d({reg1_3, reg1_2, reg1_1, reg1_0}), .dp(1'b0));
  Register #(.Bits(12)) reg_1 (
    .D({in3, in2, in1, in0, in3, in2, in1, in0, in3, in2, in1, in0}), .C(clk), .en(en_0),
    .Q({reg0_3, reg0_2, reg0_1, reg0_0, reg_1_q}));
  Register #(.Bits(12)) reg_2 (
    .D({in3, in2, in1, in0, in3, in2, in1, in0, in3, in2, in1, in0}), .C(clk), .en(en_1),
    .Q({reg1_3, reg1_2, reg1_1, reg1_0, reg_2_q}));
  Register #(.Bits(12)) reg_3 (
    .D({in3, in2, in1, in0, in3, in2, in1, in0, in3, in2, in1, in0}), .C(clk), .en(en_2),
    .Q({reg2_3, reg2_2, reg2_1, reg2_0, reg_3_q}));
  Register #(.Bits(12)) reg_4 (
    .D({in3, in2, in1, in0, in3, in2, in1, in0, in3, in2, in1, in0}), .C(clk), .en(en_3),
    .Q({reg3_3, reg3_2, reg3_1, reg3_0, reg_4_q}));
  Seven_Seg_Hex seven_seg_hex_10 (.d({2'b00, sel_readB_1, sel_readB_0}), .dp(1'b0));
  Multiplexer #(.Selector_Bits(2), .Bits(8)) multiplexer_1 (
    .sel({sel_readA_1, sel_readA_0}), .in_0(reg_1_q), .in_1(reg_2_q), .in_2(reg_3_q), .in_3(reg_4_q),
    .out({inA_3, inA_2, inA_1, inA_0, multiplexer_1_out}));
  Multiplexer #(.Selector_Bits(2), .Bits(8)) multiplexer_2 (
    .sel({sel_readB_1, sel_readB_0}), .in_0(reg_1_q), .in_1(reg_2_q), .in_2(reg_3_q), .in_3(reg_4_q),
    .out({inB_3, inB_2, inB_1, inB_0, multiplexer_2_out}));
  Seven_Seg_Hex seven_seg_hex_11 (.d({reg0_3, reg0_2, reg0_1, reg0_0}), .dp(1'b0));
  Multiplexer #(.Selector_Bits(2)) multiplexer_3 (
    .sel(multiplexer_2_out[1:0]), .in_0(multiplexer_1_out[0]), .in_1(multiplexer_1_out[1]),
    .in_2(multiplexer_1_out[2]), .in_3(multiplexer_1_out[3]), .out(out0));
  Multiplexer #(.Selector_Bits(2)) multiplexer_4 (
    .sel(multiplexer_2_out[1:0]), .in_0(multiplexer_1_out[1]), .in_1(multiplexer_1_out[2]),
    .in_2(multiplexer_1_out[3]), .in_3(multiplexer_1_out[0]), .out(out1));
  Multiplexer #(.Selector_Bits(2)) multiplexer_5 (
    .sel(multiplexer_2_out[1:0]), .in_0(multiplexer_1_out[2]), .in_1(multiplexer_1_out[3]),
    .in_2(multiplexer_1_out[0]), .in_3(multiplexer_1_out[1]), .out(out2));
  Multiplexer #(.Selector_Bits(2)) multiplexer_6 (
    .sel(multiplexer_2_out[1:0]), .in_0(multiplexer_1_out[3]), .in_1(multiplexer_1_out[0]),
    .in_2(multiplexer_1_out[1]), .in_3(multiplexer_1_out[2]), .out(out3));

  // Notes on the sheet:
  //   Interface (do not edit the content inside this box)
  //   Inputs
  //   Keypad
  //   Outputs
  //   Registers
  //   Values read into ALU inputs
  //   Rotatee
  //   Register 3
  //   Synchronizing Clock
  //   Rotation amount:
  //   Register Selection: Write-to
  //   Register 2
  //   Register Selection: Read-from
  //   ALU Output
  //   ALU input A register address:
  //   Register 1
  //   ALU input B register address:
  //   Register 0
endmodule

/* Test case:
clk in3 in2 in1 in0 sel^write_1 sel^write_0 sel^readA_1 sel^readA_0 sel^readB_1 sel^readB_0  reg3_3 reg3_2 reg3_1 reg3_0 reg2_3 reg2_2 reg2_1 reg2_0 reg1_3 reg1_2 reg1_1 reg1_0 reg0_3 reg0_2 reg0_1 reg0_0 out3 out2 out1 out0
 0   0   0   0   0   0           0           0           0           0           0            0      0      0      0      0      0      0      0      0      0      0      0      0      0      0      0      0    0    0    0
 1   0   0   0   0   0           0           0           0           0           0            0      0      0      0      0      0      0      0      0      0      0      0      0      0      0      0      0    0    0    0
 0   0   1   0   1   1           1           0           0           0           0            0      0      0      0      0      0      0      0      0      0      0      0      0      0      0      0      0    0    0    0
 1   0   1   0   1   1           1           0           0           0           0            0      1      0      1      0      0      0      0      0      0      0      0      0      0      0      0      0    0    0    0
 0   0   0   0   1   0           1           0           0           0           0            0      1      0      1      0      0      0      0      0      0      0      0      0      0      0      0      0    0    0    0
 1   0   0   0   1   0           1           0           0           0           0            0      1      0      1      0      0      0      0      0      0      0      1      0      0      0      0      0    0    0    0
 0   0   0   0   0   0           0           1           1           0           1            0      1      0      1      0      0      0      0      0      0      0      1      0      0      0      0      1    0    1    0
 1   0   0   0   0   0           0           1           1           0           1            0      1      0      1      0      0      0      0      0      0      0      1      0      0      0      0      1    0    1    0
 0   0   0   0   0   0           0           0           1           1           1            0      1      0      1      0      0      0      0      0      0      0      1      0      0      0      0      1    0    0    0
 1   0   0   0   0   0           0           0           1           1           1            0      1      0      1      0      0      0      0      0      0      0      1      0      0      0      0      1    0    0    0
*/
