// Digital circuit part_c.dig as structural Verilog
module part_c (
  input  in_0,
  input  in_2,
  input  in_1,
  output out_0
);

  wire nfet_5_s, nfet_8_d, pfet_1_d, pfet_2_d, pfet_3_d, pfet_4_d, pfet_5_d, pfet_6_d, pfet_7_d, pfet_9_d,
       pfet_10_d;

  PFET pfet_1 (.G(in_1), .S(1'b1), .D(pfet_1_d));
  NFET nfet_1 (.G(in_1), .D(pfet_1_d), .S(1'b0));
  PFET pfet_2 (.G(pfet_1_d), .S(1'b1), .D(pfet_2_d));
  PFET pfet_3 (.G(in_2), .S(pfet_2_d), .D(pfet_3_d));
  NFET nfet_2 (.G(in_2), .D(pfet_3_d), .S(1'b0));
  FGNFET fgnfet_1 (.G(pfet_1_d), .D(pfet_3_d), .S(1'b0));
  PFET pfet_4 (.G(pfet_3_d), .S(1'b1), .D(pfet_4_d));
  NFET nfet_3 (.G(pfet_3_d), .D(pfet_4_d), .S(1'b0));
  PFET pfet_5 (.G(in_0), .S(1'b1), .D(pfet_5_d));
  PFET pfet_6 (.G(in_2), .S(pfet_5_d), .D(pfet_6_d));
  NFET nfet_4 (.G(in_2), .D(pfet_6_d), .S(1'b0));
  PFET pfet_7 (.G(in_0), .S(1'b1), .D(pfet_7_d));
  FGNFET fgnfet_2 (.G(in_0), .D(pfet_6_d), .S(1'b0));
  NFET nfet_5 (.G(in_0), .D(pfet_7_d), .S(nfet_5_s));
  NFET nfet_6 (.G(pfet_4_d), .D(nfet_5_s), .S(1'b0));
  PFET pfet_8 (.G(pfet_4_d), .S(1'b1), .D(pfet_7_d));
  PFET pfet_9 (.G(pfet_7_d), .S(1'b1), .D(pfet_9_d));
  NFET nfet_7 (.G(pfet_7_d), .D(pfet_9_d), .S(1'b0));
  NFET nfet_8 (.G(pfet_9_d), .D(nfet_8_d), .S(1'b0));
  PFET pfet_10 (.G(pfet_6_d), .S(1'b1), .D(pfet_10_d));
  PFET pfet_11 (.G(pfet_9_d), .S(pfet_10_d), .D(nfet_8_d));
  FGNFET fgnfet_3 (.G(pfet_6_d), .D(nfet_8_d), .S(1'b0));
  PFET pfet_12 (.G(nfet_8_d), .S(1'b1), .D(out_0));
  NFET nfet_9 (.G(nfet_8_d), .D(out_0), .S(1'b0));
endmodule

/* Test case part_c_test:
in_0 in_1 in_2 out_0
 0    0    0    1
 0    0    1    0
 0    1    0    1
 0    1    1    0
 1    0    0    1
 1    0    1    1
 1    1    0    0
 1    1    1    1
*/
